// Logisim project CPU.circ as structural Verilog
module log8old (
);

  wire button_1_out, clock_1_out;
  wire [1:0] demultiplexer_1_out0, demultiplexer_1_out1, demultiplexer_1_out2, demultiplexer_1_out3,
       demultiplexer_1_out4, demultiplexer_1_out5, demultiplexer_1_out6, demultiplexer_1_out7, rom_1_data_5;
  wire [2:0] rom_1_data_3;
  wire [3:0] alu_1_p3, and_1_out, counter_1_q, register_5_q, rom_1_data_2;
  wire [5:3] rom_1_data_4;
  wire [6:0] pull_resistor_1_node;
  wire [7:0] ACC_q, alu_1_p5, controlled_buffer_1_out, controlled_buffer_2_out, multiplexer_1_out,
       register_1_q, register_2_q, register_3_q, register_4_q, register_6_q, register_7_q, register_8_q,
       register_9_q;
  wire [8:8] or_1_out;
  wire [15:0] controlled_buffer_7_out, pull_resistor_2_node;
  wire [23:0] rom_1_data;

  Demultiplexer #(.select(3), .width(2)) demultiplexer_1 (
    .out0(demultiplexer_1_out0), .out1(demultiplexer_1_out1), .out2(demultiplexer_1_out2),
    .out3(demultiplexer_1_out3), .out4(demultiplexer_1_out4), .out5(demultiplexer_1_out5),
    .out6(demultiplexer_1_out6), .out7(demultiplexer_1_out7), .in(rom_1_data_4[4:3]), .sel(rom_1_data_3));
  Counter #(.max('hf), .trigger("falling"), .width(4)) counter_1 (
    .Q(counter_1_q), .clk(clock_1_out));  // open: load, D, count, carry, up, clr
  Clock clock_1 (.out(clock_1_out));
  Register register_1 (
    .D(controlled_buffer_1_out), .en(demultiplexer_1_out4[0]), .Q(register_1_q), .clk(clock_1_out));  // open: clr
  // Probe on controlled_buffer_2_out
  Register register_2 (
    .D(controlled_buffer_2_out), .en(demultiplexer_1_out1[0]), .Q(register_2_q), .clk(clock_1_out));  // open: clr
  assign controlled_buffer_1_out = demultiplexer_1_out4[1] ? register_1_q : 8'bz;  // Controlled_Buffer controlled_buffer_1
  Register register_3 (
    .D(controlled_buffer_1_out), .en(demultiplexer_1_out5[0]), .Q(register_3_q), .clk(clock_1_out));  // open: clr
  Register register_4 (
    .D(controlled_buffer_2_out), .en(rom_1_data_5[0]), .Q(register_4_q), .clk(clock_1_out));  // open: clr
  Register #(.width(4)) register_5 (
    .D(alu_1_p3), .en(rom_1_data_5[1]), .Q(register_5_q), .clk(clock_1_out));  // open: clr
  assign controlled_buffer_2_out = demultiplexer_1_out1[1] ? register_2_q : 8'bz;  // Controlled_Buffer controlled_buffer_2
  Register register_6 (
    .D(controlled_buffer_2_out), .en(demultiplexer_1_out2[0]), .Q(register_6_q), .clk(clock_1_out));  // open: clr
  assign controlled_buffer_1_out = demultiplexer_1_out5[1] ? register_3_q : 8'bz;  // Controlled_Buffer controlled_buffer_3
  Register register_7 (
    .D(controlled_buffer_1_out), .en(demultiplexer_1_out6[0]), .Q(register_7_q), .clk(clock_1_out));  // open: clr
  assign and_1_out = register_4_q[3:0] & register_5_q;  // AND_Gate and_1, 4 bits wide
  or or_1 (or_1_out[8], and_1_out[0], and_1_out[1], and_1_out[2], and_1_out[3]);
  assign controlled_buffer_2_out = demultiplexer_1_out2[1] ? register_6_q : 8'bz;  // Controlled_Buffer controlled_buffer_4
  Register register_8 (
    .D(controlled_buffer_2_out), .en(demultiplexer_1_out3[0]), .Q(register_8_q), .clk(clock_1_out));  // open: clr
  assign controlled_buffer_1_out = demultiplexer_1_out6[1] ? register_7_q : 8'bz;  // Controlled_Buffer controlled_buffer_5
  Register register_9 (
    .D(controlled_buffer_1_out), .en(demultiplexer_1_out7[0]), .Q(register_9_q), .clk(clock_1_out));  // open: clr
  ROM #(.addrWidth(16), .dataWidth(24)) rom_1 (
    .addr({pull_resistor_1_node, or_1_out[8], register_4_q[7:4], counter_1_q}),
    .data({rom_1_data[23:21], rom_1_data_5, rom_1_data_4, rom_1_data_3, rom_1_data_2, rom_1_data[8:0]}));
  Pull_Resistor pull_resistor_1 (.node(pull_resistor_1_node));
  // Probe on nothing
  assign controlled_buffer_2_out = demultiplexer_1_out3[1] ? register_8_q : 8'bz;  // Controlled_Buffer controlled_buffer_6
  assign controlled_buffer_7_out = rom_1_data_4[5] ? {register_9_q, register_7_q} : 16'bz;  // Controlled_Buffer controlled_buffer_7
  assign controlled_buffer_1_out = demultiplexer_1_out7[1] ? register_9_q : 8'bz;  // Controlled_Buffer controlled_buffer_8
  // Probe on controlled_buffer_7_out
  // Probe on controlled_buffer_2_out
  // Probe on controlled_buffer_2_out
  // Probe on controlled_buffer_2_out
  PC pc_1 ();  // open: IN8, Clk, CTLDE8E16, ProbeOut, OUT8, OUT16
  RAM #(.addrWidth(16), .clearpin("true"), .databus("bidir")) ram_1 (
    .addr(pull_resistor_2_node), .we(rom_1_data[7]), .oe(rom_1_data[8]), .clk(clock_1_out),
    .data(controlled_buffer_2_out), .clr(button_1_out));
  Pull_Resistor pull_resistor_2 (.node(pull_resistor_2_node));
  assign pull_resistor_2_node = controlled_buffer_7_out;  // Buffer buffer_1, 16 bits wide
  // Probe on alu_1_p5
  // Probe on alu_1_p3
  Button button_1 (.out(button_1_out));
  Multiplexer #(.width(8)) multiplexer_1 (
    .in0(alu_1_p5), .in1(controlled_buffer_2_out), .out(multiplexer_1_out), .sel(rom_1_data[6]));
  assign controlled_buffer_2_out = rom_1_data[5] ? ACC_q : 8'bz;  // Controlled_Buffer controlled_buffer_9
  Register ACC (.D(multiplexer_1_out), .en(rom_1_data[4]), .Q(ACC_q), .clk(clock_1_out));  // open: clr
  // ALU alu_1: pin names not known; wires that end beside it: rom_1_data[3], rom_1_data[2:0], alu_1_p3, controlled_buffer_2_out, alu_1_p5, ACC_q

  // Notes on the sheet:
  //   contents of rom_1 (hex, n*v repeats v):
  //   1240 10240
endmodule

module PC (
  input  [7:0] IN8,
  input  Clk,
  input  [3:0] CTLDE8E16,
  output [15:0] ProbeOut,
  output [15:0] OUT16,
  output [7:0] OUT8
);

  wire and_1_out, and_2_out, and_3_out, counter_1_carry, not_1_out, not_2_out;

  not not_1 (not_1_out, CTLDE8E16[3]);
  not not_2 (not_2_out, CTLDE8E16[2]);
  and and_1 (and_1_out, CTLDE8E16[3], not_2_out);
  and and_2 (and_2_out, not_1_out, CTLDE8E16[2]);
  Counter counter_1 (
    .load(and_2_out), .D(IN8), .count(CTLDE8E16[3]), .Q(ProbeOut[7:0]), .carry(counter_1_carry),
    .up(and_1_out), .clk(Clk));  // open: clr
  Counter counter_2 (
    .load(and_2_out), .D(ProbeOut[7:0]), .count(and_3_out), .Q(ProbeOut[15:8]), .up(and_1_out), .clk(Clk));  // open: carry, clr
  and and_3 (and_3_out, counter_1_carry, CTLDE8E16[3]);
  assign OUT16 = CTLDE8E16[0] ? ProbeOut : 16'bz;  // Controlled_Buffer controlled_buffer_1
  assign OUT8 = CTLDE8E16[1] ? ProbeOut[15:8] : 8'bz;  // Controlled_Buffer controlled_buffer_2

  // Notes on the sheet:
  //   Clk: pull=down
  //   CTLDE8E16: pull=down
endmodule

module ALU (
  input  [2:0] OP,
  input  [7:0] A_IN,
  input  [7:0] B_IN,
  input  C_IN,
  output [7:0] ALU_OUT,
  output [3:0] FLG_OUT
);

  wire [3:3] pull_resistor_1_node;
  wire [7:0] adder_1_out, and_1_out, demultiplexer_1_out0, demultiplexer_1_out1, demultiplexer_1_out2,
       demultiplexer_1_out3, demultiplexer_1_out4, demultiplexer_1_out5, demultiplexer_1_out6,
       demultiplexer_1_out7, demultiplexer_2_out0, demultiplexer_2_out1, demultiplexer_2_out2,
       demultiplexer_2_out3, demultiplexer_2_out4, demultiplexer_2_out5, demultiplexer_2_out6,
       demultiplexer_2_out7, not_1_out, or_1_out, shifter_1_out, shifter_2_out, xor_1_out;

  Demultiplexer #(.select(3), .width(8)) demultiplexer_1 (
    .out0(demultiplexer_1_out0), .out1(demultiplexer_1_out1), .out2(demultiplexer_1_out2),
    .out3(demultiplexer_1_out3), .out4(demultiplexer_1_out4), .out5(demultiplexer_1_out5),
    .out6(demultiplexer_1_out6), .out7(demultiplexer_1_out7), .in(A_IN), .sel(OP));
  Demultiplexer #(.select(3), .width(8)) demultiplexer_2 (
    .out0(demultiplexer_2_out0), .out1(demultiplexer_2_out1), .out2(demultiplexer_2_out2),
    .out3(demultiplexer_2_out3), .out4(demultiplexer_2_out4), .out5(demultiplexer_2_out5),
    .out6(demultiplexer_2_out6), .out7(demultiplexer_2_out7), .in(B_IN), .sel(OP));
  Adder adder_1 (.a(demultiplexer_1_out0), .b(demultiplexer_2_out0), .out(adder_1_out), .cin(C_IN), .cout(FLG_OUT[3]));
  Shifter shifter_1 (.in(demultiplexer_1_out1), .\dist (demultiplexer_2_out1[2:0]), .out(shifter_1_out));
  Shifter #(.shift("lr")) shifter_2 (
    .in(demultiplexer_1_out2), .\dist (demultiplexer_2_out2[2:0]), .out(shifter_2_out));
  assign not_1_out = ~demultiplexer_2_out3;  // NOT_Gate not_1, 8 bits wide
  assign and_1_out = demultiplexer_1_out4 & demultiplexer_2_out4;  // AND_Gate and_1, 8 bits wide
  assign or_1_out = demultiplexer_1_out5 | demultiplexer_2_out5;  // OR_Gate or_1, 8 bits wide
  assign xor_1_out = demultiplexer_1_out6 ^ demultiplexer_2_out6;  // XOR_Gate xor_1, 8 bits wide
  Comparator #(.mode("unsigned")) comparator_1 (
    .a(demultiplexer_1_out7), .b(demultiplexer_2_out7), .gt(FLG_OUT[1]), .eq(FLG_OUT[2]));  // open: lt
  or or_2 (FLG_OUT[0], demultiplexer_1_out7[0], demultiplexer_1_out7[1], demultiplexer_1_out7[2], demultiplexer_1_out7[3], demultiplexer_1_out7[4], demultiplexer_1_out7[5], demultiplexer_1_out7[6], demultiplexer_1_out7[7]);
  Pull_Resistor pull_resistor_1 (.node(pull_resistor_1_node[3]));
  Multiplexer #(.select(3), .width(8)) multiplexer_1 (
    .in0(adder_1_out), .in1(shifter_1_out), .in2(shifter_2_out), .in3(not_1_out), .in4(and_1_out),
    .in5(or_1_out), .in6(xor_1_out), .out(ALU_OUT), .sel(OP));  // open: in7

  // Notes on the sheet:
  //   OP: pull=down
endmodule

module Breadboard (
  input  in_1,
  input  in_2,
  input  in_3,
  input  in_4,
  input  [2:0] in_5
);

  wire alu_1_p3, undriven_2;
  wire [7:0] ACC_q, controlled_buffer_1_out, multiplexer_1_out, undriven;

  // Probe on undriven
  // Probe on alu_1_p3
  Multiplexer #(.width(8)) multiplexer_1 (
    .in0(controlled_buffer_1_out), .in1(undriven), .out(multiplexer_1_out), .sel(in_1));
  Register ACC (.D(multiplexer_1_out), .en(in_2), .Q(ACC_q), .clk(undriven_2));  // open: clr
  assign controlled_buffer_1_out = in_3 ? ACC_q : 8'bz;  // Controlled_Buffer controlled_buffer_1
  // ALU alu_1: pin names not known; wires that end beside it: in_4, in_5, alu_1_p3, controlled_buffer_1_out, ACC_q
endmodule

module log8 (
  output [7:0] out_1
);

  wire and_1_out, clock_1_out, counter_2_carry, not_1_out;
  wire [0:0] rom_1_data_3;
  wire [1:0] demultiplexer_1_out0, demultiplexer_1_out1, demultiplexer_1_out2, demultiplexer_1_out3,
       rom_1_data_4, rom_1_data_5, rom_1_data_6;
  wire [3:0] alu_1_flg_out, counter_1_q, pull_resistor_1_node;
  wire [4:0] rom_1_data_2;
  wire [5:0] rom_1_data_7;
  wire [7:0] ACC_q, alu_1_alu_out, controlled_buffer_1_out, counter_2_q, counter_3_q, multiplexer_1_out,
       register_1_q, register_2_q, register_3_q, register_4_q, register_6_q, register_7_q, register_8_q,
       TMP_q;
  wire [15:0] controlled_buffer_4_out;
  wire [25:0] rom_1_data;

  assign controlled_buffer_1_out = demultiplexer_1_out3[0] ? register_1_q : 8'bz;  // Controlled_Buffer controlled_buffer_1
  Register register_1 (
    .D(controlled_buffer_1_out), .en(demultiplexer_1_out3[1]), .Q(register_1_q), .clk(clock_1_out));  // open: clr
  assign controlled_buffer_1_out = demultiplexer_1_out2[0] ? register_2_q : 8'bz;  // Controlled_Buffer controlled_buffer_2
  Register register_2 (
    .D(controlled_buffer_1_out), .en(demultiplexer_1_out2[1]), .Q(register_2_q), .clk(clock_1_out));  // open: clr
  assign controlled_buffer_1_out = demultiplexer_1_out1[0] ? register_3_q : 8'bz;  // Controlled_Buffer controlled_buffer_3
  Register register_3 (
    .D(controlled_buffer_1_out), .en(demultiplexer_1_out1[1]), .Q(register_3_q), .clk(clock_1_out));  // open: clr
  Register register_4 (
    .D(controlled_buffer_1_out), .en(demultiplexer_1_out0[1]), .Q(register_4_q), .clk(clock_1_out));  // open: clr
  Register register_5 (.D(controlled_buffer_1_out), .en(rom_1_data[25]), .Q(out_1), .clk(clock_1_out));  // open: clr
  and and_1 (and_1_out, rom_1_data_6[0], clock_1_out);
  Counter #(.max('hf), .width(4)) counter_1 (
    .Q(counter_1_q), .clk(clock_1_out), .clr(and_1_out));  // open: load, D, count, carry, up
  Register register_6 (
    .D(controlled_buffer_1_out), .en(rom_1_data_6[1]), .Q(register_6_q), .clk(clock_1_out));  // open: clr
  Clock clock_1 (.out(clock_1_out));
  assign controlled_buffer_4_out = rom_1_data_3[0] ? {register_4_q, register_3_q} : 16'bz;  // Controlled_Buffer controlled_buffer_4
  assign controlled_buffer_1_out = demultiplexer_1_out0[0] ? register_4_q : 8'bz;  // Controlled_Buffer controlled_buffer_5
  Demultiplexer #(.select(2), .width(2)) demultiplexer_1 (
    .out0(demultiplexer_1_out0), .out1(demultiplexer_1_out1), .out2(demultiplexer_1_out2),
    .out3(demultiplexer_1_out3), .in(rom_1_data_4), .sel(rom_1_data_5));
  Pull_Resistor pull_resistor_1 (.node(pull_resistor_1_node));
  // Probe on controlled_buffer_4_out
  // Probe on controlled_buffer_1_out
  ROM #(.addrWidth(16), .dataWidth(32)) rom_1 (
    .addr({pull_resistor_1_node, register_6_q, counter_1_q}),
    .data({rom_1_data_7, rom_1_data[25], rom_1_data_6, rom_1_data_5, rom_1_data_4, rom_1_data_3[0], rom_1_data[17:15], rom_1_data_2, rom_1_data[9:0]}));
  Register register_7 (
    .D(controlled_buffer_1_out), .en(rom_1_data[15]), .Q(register_7_q), .clk(clock_1_out));  // open: clr
  not not_1 (not_1_out, rom_1_data_2[0]);
  Counter counter_2 (
    .load(rom_1_data_2[1]), .D(controlled_buffer_1_out), .count(rom_1_data_2[2]), .Q(counter_2_q),
    .carry(counter_2_carry), .up(not_1_out), .clk(clock_1_out));  // open: clr
  assign controlled_buffer_1_out = rom_1_data[16] ? register_8_q : 8'bz;  // Controlled_Buffer controlled_buffer_6
  Register register_8 (.D(register_7_q), .en(rom_1_data[15]), .Q(register_8_q), .clk(clock_1_out));  // open: clr
  assign controlled_buffer_1_out = rom_1_data_2[4] ? counter_3_q : 8'bz;  // Controlled_Buffer controlled_buffer_7
  Counter counter_3 (
    .load(rom_1_data_2[1]), .D(counter_2_q), .count(counter_2_carry), .Q(counter_3_q), .up(not_1_out),
    .clk(clock_1_out));  // open: carry, clr
  assign controlled_buffer_4_out = rom_1_data[17] ? {register_8_q, register_7_q} : 16'bz;  // Controlled_Buffer controlled_buffer_8
  assign controlled_buffer_4_out = rom_1_data_2[3] ? {counter_3_q, counter_2_q} : 16'bz;  // Controlled_Buffer controlled_buffer_9
  Multiplexer #(.width(8)) multiplexer_1 (
    .in0(alu_1_alu_out), .in1(controlled_buffer_1_out), .out(multiplexer_1_out), .sel(rom_1_data[4]));
  Register ACC (.D(multiplexer_1_out), .en(rom_1_data[5]), .Q(ACC_q), .clk(clock_1_out));  // open: clr
  // Probe on alu_1_alu_out
  // Probe on alu_1_flg_out
  RAM #(.addrWidth(16), .databus("bidir")) ram_1 (
    .addr(controlled_buffer_4_out), .we(rom_1_data[8]), .oe(rom_1_data[9]), .clk(clock_1_out),
    .data(controlled_buffer_1_out));
  assign controlled_buffer_1_out = rom_1_data[6] ? ACC_q : 8'bz;  // Controlled_Buffer controlled_buffer_10
  Register TMP (.D(controlled_buffer_1_out), .en(rom_1_data[7]), .Q(TMP_q), .clk(clock_1_out));  // open: clr
  ALU alu_1 (
    .A_IN(ACC_q), .OP(rom_1_data[3:1]), .B_IN(TMP_q), .C_IN(rom_1_data[0]), .FLG_OUT(alu_1_flg_out),
    .ALU_OUT(alu_1_alu_out));
endmodule
