// Logisim project CPU2.circ as structural Verilog: 9 circuits, main circuit mboard
module mboard (
  input  in_1,
  input  in_2
);

  wire and_1_out, and_2_out, and_3_out, and_4_out, buffer_2_out, buffer_3_out, clock_1_out, decoder_1_out0,
       decoder_2_out0, log8_1_we, not_1_out, not_2_out, not_3_out;
  wire [7:0] log8_1_out8, ram_1_data, rom_1_data;
  wire [13:0] controlled_buffer_3_out;
  wire [15:0] log8_1_out16, pull_resistor_1_node;

  Clock clock_1 (.out(clock_1_out));
  LOG8 log8_1 (
    .HLT(in_2), .Int(in_1), .IN8(log8_1_out8), .Clk(clock_1_out), .OUT16(log8_1_out16), .OUT8(log8_1_out8),
    .WE(log8_1_we));
  // Probe on log8_1_out16
  // Probe on log8_1_out8
  Pull_Resistor pull_resistor_1 (.node(pull_resistor_1_node));
  assign pull_resistor_1_node = log8_1_out16;  // Buffer buffer_1, 16 bits wide
  not not_1 (not_1_out, pull_resistor_1_node[15]);
  buf buffer_2 (buffer_2_out, pull_resistor_1_node[15]);
  Pull_Resistor pull_resistor_2 (.node(buffer_2_out));
  Decoder decoder_1 (.out0(decoder_1_out0), .sel(buffer_2_out), .en(pull_resistor_1_node[15]));  // open: out1
  not not_2 (not_2_out, decoder_1_out0);
  buf buffer_3 (buffer_3_out, log8_1_out16[15]);
  Pull_Resistor pull_resistor_3 (.node(buffer_3_out));
  Decoder decoder_2 (.out0(decoder_2_out0), .sel(buffer_3_out), .en(log8_1_out16[15]));  // open: out1
  and and_1 (and_1_out, and_2_out, ~log8_1_we);  // AND_Gate
  and and_2 (and_2_out, not_1_out, not_2_out);
  and and_3 (and_3_out, and_2_out, log8_1_we);
  assign log8_1_out8 = and_1_out ? ram_1_data : 8'bz;  // Controlled_Buffer controlled_buffer_1
  and and_4 (and_4_out, log8_1_out16[14], not_3_out, log8_1_out16[15]);
  not not_3 (not_3_out, decoder_2_out0);
  RAM #(.addrWidth(15), .databus("bidir"), .enables("line")) ram_1 (
    .addr(pull_resistor_1_node[14:0]), .data(ram_1_data));  // open: we, oe, clk
  assign ram_1_data = and_3_out ? log8_1_out8 : 8'bz;  // Controlled_Buffer controlled_buffer_2
  ROM #(.addrWidth(14)) rom_1 (.addr(controlled_buffer_3_out), .data(rom_1_data));
  assign controlled_buffer_3_out = and_4_out ? log8_1_out16[13:0] : 14'bz;  // Controlled_Buffer controlled_buffer_3
  assign log8_1_out8 = and_4_out ? rom_1_data : 8'bz;  // Controlled_Buffer controlled_buffer_4

  // Notes on the sheet:
  //   RAM
  //   RAM
  //   RAM
  //   RAM
  //   ROM
  //   ROM
  //   RAMSPACE:
  //   0
  //   8k
  //   16k
  //   24k
  //   32k
  //   40k
  //   48k
  //   56k
  //   64k
  //   0x0000
  //   0x2000
  //   0x4000
  //   0x6000
  //   0x8000
  //   0xa000
  //   0xc000
  //   0xe000
  //   0xffff
  //   contents of rom_1 (hex, n*v repeats v):
  //   15 0 ff 8188*0 c0 7936*0 a0 254*0 c0
endmodule

module LOG8 (
  input  [7:0] IN8,
  input  Clk,
  input  Int,
  input  HLT,
  output [15:0] OUT16,
  output WE,
  output [7:0] OUT8
);

  wire and_2_out, and_3_out, INTFLG_q, nor_1_out, not_1_out, not_2_out, not_3_out, or_2_out, t_ff_1_q;
  wire [1:0] demultiplexer_2_out0, demultiplexer_2_out1, demultiplexer_2_out2, demultiplexer_2_out3,
       demultiplexer_3_out0, demultiplexer_3_out1, demultiplexer_3_out2, demultiplexer_3_out3,
       multiplexer_1_out_4, multiplexer_1_out_5, or_3_out, or_4_out, or_5_out, or_6_out;
  wire [2:0] CTR_q, demultiplexer_1_out0, demultiplexer_1_out1;
  wire [3:0] alu_1_z, ALUFLG_q, and_1_out, decoder_1_out3, multiplexer_1_out;
  wire [4:0] pla_1_out;
  wire [5:0] pull_resistor_4_node;
  wire [7:0] buffer_1_out, controlled_buffer_3_out, INR_q, multiplexer_1_out_3, multiplexer_2_out,
       multiplexer_3_out, register_1_q, register_2_q, register_3_q, register_4_q, register_5_q, register_6_q;
  wire [9:0] counter_2_q;
  wire [9:9] or_1_out;
  wire [15:0] controlled_buffer_2_out, counter_1_q;
  wire [63:0] rom_1_data, rom_2_data;
  wire [63:5] multiplexer_1_out_2;

  Register INR (.D(controlled_buffer_3_out), .en(multiplexer_1_out[2]), .Q(INR_q), .clk(Clk));  // open: clr
  Register #(.width(4)) ALUFLG (.D(alu_1_z), .en(multiplexer_1_out[3]), .Q(ALUFLG_q), .clk(Clk));  // open: clr
  Decoder #(.enable("false"), .select(2)) decoder_1 (
    .out0(decoder_1_out3[3]), .out1(decoder_1_out3[2]), .out2(decoder_1_out3[1]), .out3(decoder_1_out3[0]),
    .sel(INR_q[1:0]));
  not not_1 (not_1_out, HLT);
  not not_2 (not_2_out, multiplexer_1_out[1]);
  assign and_1_out = decoder_1_out3 & ALUFLG_q;  // AND_Gate and_1, 4 bits wide
  or or_1 (or_1_out[9], and_1_out[0], and_1_out[1], and_1_out[2], and_1_out[3]);
  Demultiplexer #(.width(3)) demultiplexer_1 (
    .out0(demultiplexer_1_out0), .out1(demultiplexer_1_out1), .in(CTR_q), .sel(t_ff_1_q));
  Counter #(.max('h7), .ongoal("stay"), .trigger("falling"), .width(3)) CTR (
    .count(not_1_out), .Q(CTR_q), .clk(Clk), .clr(nor_1_out));  // open: load, D, carry, up
  nor nor_1 (nor_1_out, multiplexer_1_out[1], not_2_out);
  T_Flip_Flop INTFLG (.clk(Clk), .T(multiplexer_1_out[0]), .Q(INTFLG_q));  // open: Qn, preset, reset
  ROM #(.addrWidth(4), .dataWidth(64)) rom_1 (.addr({Int, demultiplexer_1_out0}), .data(rom_1_data));
  ROM #(.addrWidth(10), .dataWidth(64)) rom_2 (
    .addr({or_1_out[9], INR_q[7:2], demultiplexer_1_out1}), .data(rom_2_data));
  Demultiplexer #(.select(2), .width(2)) demultiplexer_2 (
    .out0(demultiplexer_2_out0), .out1(demultiplexer_2_out1), .out2(demultiplexer_2_out2),
    .out3(demultiplexer_2_out3), .in(multiplexer_1_out_5), .sel(INR_q[1:0]));
  and and_2 (and_2_out, ~t_ff_1_q, multiplexer_1_out[1]);  // AND_Gate
  and and_3 (and_3_out, t_ff_1_q, multiplexer_1_out[1], Int, INTFLG_q);
  Demultiplexer #(.select(2), .width(2)) demultiplexer_3 (
    .out0(demultiplexer_3_out0), .out1(demultiplexer_3_out1), .out2(demultiplexer_3_out2),
    .out3(demultiplexer_3_out3), .in(multiplexer_1_out_4), .sel(INR_q[3:2]));
  T_Flip_Flop #(.trigger("falling")) t_ff_1 (.clk(Clk), .T(or_2_out), .Q(t_ff_1_q));  // open: Qn, preset, reset
  or or_2 (or_2_out, and_2_out, and_3_out);
  assign or_3_out = demultiplexer_3_out0 | demultiplexer_2_out0;  // OR_Gate or_3, 2 bits wide
  assign or_4_out = demultiplexer_3_out1 | demultiplexer_2_out1;  // OR_Gate or_4, 2 bits wide
  assign or_5_out = demultiplexer_3_out2 | demultiplexer_2_out2;  // OR_Gate or_5, 2 bits wide
  assign or_6_out = demultiplexer_3_out3 | demultiplexer_2_out3;  // OR_Gate or_6, 2 bits wide
  Multiplexer #(.width(64)) multiplexer_1 (
    .in0(rom_1_data), .in1(rom_2_data),
    .out({multiplexer_1_out_2[63:32], multiplexer_1_out_5, multiplexer_1_out_4, multiplexer_1_out_2[27:16], multiplexer_1_out_3, multiplexer_1_out_2[7:5], multiplexer_1_out, WE}),
    .sel(t_ff_1_q));
  // Probe on Clk
  // Probe on controlled_buffer_3_out
  // Probe on controlled_buffer_2_out
  assign OUT16 = multiplexer_1_out_2[22] ? controlled_buffer_2_out : 16'bz;  // Controlled_Buffer controlled_buffer_1
  PLA #(.in_width(3), .out_width(5), .\table ("001 00111\n010 11001\n100 00010\n101 00100\n110 01000\n111 10000\n000 00000")) pla_1 (
    .in(multiplexer_1_out_2[7:5]), .out(pla_1_out));
  assign controlled_buffer_2_out = multiplexer_1_out_2[27] ? {{13{1'b1}}, multiplexer_1_out_2[26:24]} : 16'bz;  // Controlled_Buffer controlled_buffer_2
  Pull_Resistor pull_resistor_1 (.node({multiplexer_1_out_2[63:32], multiplexer_1_out_5, multiplexer_1_out_4, multiplexer_1_out_2[27:16], multiplexer_1_out_3, multiplexer_1_out_2[7:5], multiplexer_1_out, WE}));
  Pull_Resistor pull_resistor_2 (.node(IN8));
  assign controlled_buffer_3_out = not_3_out ? IN8 : 8'bz;  // Controlled_Buffer controlled_buffer_3
  not not_3 (not_3_out, WE);
  assign buffer_1_out = controlled_buffer_3_out;  // Buffer buffer_1, 8 bits wide
  assign OUT8 = WE ? buffer_1_out : 8'bz;  // Controlled_Buffer controlled_buffer_4
  Pull_Resistor pull_resistor_3 (.node(buffer_1_out));
  Multiplexer #(.width(8)) multiplexer_2 (
    .in0(controlled_buffer_3_out), .in1(controlled_buffer_2_out[7:0]), .out(multiplexer_2_out),
    .sel(pla_1_out[0]));
  assign controlled_buffer_2_out = multiplexer_1_out_3[3] ? counter_1_q : 16'bz;  // Controlled_Buffer controlled_buffer_5
  Counter #(.max('hffff), .width(16)) counter_1 (
    .load(multiplexer_1_out_3[1]), .D(controlled_buffer_2_out), .count(multiplexer_1_out_3[2]),
    .Q(counter_1_q), .up(multiplexer_1_out_3[0]), .clk(Clk));  // open: carry, clr
  Counter #(.max('h3ff), .width(10)) counter_2 (
    .load(multiplexer_1_out_3[5]), .D(controlled_buffer_2_out[9:0]), .count(multiplexer_1_out_3[6]),
    .Q(counter_2_q), .up(multiplexer_1_out_3[4]), .clk(Clk));  // open: carry, clr
  assign controlled_buffer_2_out = multiplexer_1_out_3[7] ? {pull_resistor_4_node, counter_2_q} : 16'bz;  // Controlled_Buffer controlled_buffer_6
  Pull_Resistor pull_resistor_4 (.node(pull_resistor_4_node));
  assign controlled_buffer_3_out = or_3_out[1] ? register_1_q : 8'bz;  // Controlled_Buffer controlled_buffer_7
  Register register_1 (.D(controlled_buffer_3_out), .en(or_3_out[0]), .Q(register_1_q), .clk(Clk));  // open: clr
  assign controlled_buffer_3_out = or_5_out[1] ? register_2_q : 8'bz;  // Controlled_Buffer controlled_buffer_8
  Register register_2 (.D(controlled_buffer_3_out), .en(or_5_out[0]), .Q(register_2_q), .clk(Clk));  // open: clr
  ALU alu_1 (
    .A(register_2_q), .B(register_5_q), .cin(multiplexer_1_out_2[21]), .op3(multiplexer_1_out_2[20]),
    .op2(multiplexer_1_out_2[19]), .op1(multiplexer_1_out_2[18]), .op0(multiplexer_1_out_2[17]),
    .X(multiplexer_1_out_2[16]), .O(controlled_buffer_3_out), .Z(alu_1_z[0]), .G(alu_1_z[1]), .E(alu_1_z[2]),
    .C(alu_1_z[3]));
  Demultiplexer #(.disabled("Z"), .enable("true"), .tristate("true"), .width(8)) demultiplexer_4 (
    .out0(controlled_buffer_3_out), .out1(controlled_buffer_2_out[7:0]), .in(register_3_q),
    .sel(pla_1_out[0]), .en(pla_1_out[3]));
  Register register_3 (.D(multiplexer_2_out), .en(pla_1_out[1]), .Q(register_3_q), .clk(Clk));  // open: clr
  assign controlled_buffer_3_out = or_4_out[1] ? register_4_q : 8'bz;  // Controlled_Buffer controlled_buffer_9
  Register register_4 (.D(controlled_buffer_3_out), .en(or_4_out[0]), .Q(register_4_q), .clk(Clk));  // open: clr
  assign controlled_buffer_3_out = or_6_out[1] ? register_5_q : 8'bz;  // Controlled_Buffer controlled_buffer_10
  Register register_5 (.D(controlled_buffer_3_out), .en(or_6_out[0]), .Q(register_5_q), .clk(Clk));  // open: clr
  Multiplexer #(.width(8)) multiplexer_3 (
    .in0(controlled_buffer_3_out), .in1(controlled_buffer_2_out[15:8]), .out(multiplexer_3_out),
    .sel(pla_1_out[0]));
  Demultiplexer #(.disabled("Z"), .enable("true"), .tristate("true"), .width(8)) demultiplexer_5 (
    .out0(controlled_buffer_3_out), .out1(controlled_buffer_2_out[15:8]), .in(register_6_q),
    .sel(pla_1_out[0]), .en(pla_1_out[4]));
  Register register_6 (.D(multiplexer_3_out), .en(pla_1_out[2]), .Q(register_6_q), .clk(Clk));  // open: clr

  // Notes on the sheet:
  //   contents of rom_1 (hex, n*v repeats v):
  //   e400080 f4000a0 4246 5*0 820 40c0c1 40c0e1 c400080 d4000a0 244
  //   contents of rom_2 (hex, n*v repeats v):
  //   400d08 4 6*0 400d08 4 6*0 400d08 4 6*0 400d08 4 6*0 400d08 40400d04 6*0 400d08 400d80 400da0
  //   40400044 4*0 400d08 4 6*0 400d08 4 6*0 400d08 4 6*0 400d08 4 6*0 400d08 4 6*0 400d08 4 6*0 400d08 4
  //   6*0 400d08 4 6*0 400d08 4 6*0 400d08 4 6*0 400d08 4 6*0 400d08 4 6*0 400d08 4 6*0 400d08 4 6*0
  //   400d08 4 6*0 400d08 4 6*0 400d08 4 6*0 400d08 4 6*0 400d08 4 6*0 400d08 4 6*0 400d08 4 6*0 400d08 4
  //   6*0 400d08 4 6*0 400d08 4 6*0 400d08 4 6*0 400d08 4 6*0 400d08 4 6*0 400d08 4 6*0 400d08 4 6*0
  //   400d08 4 6*0 400d08 4 6*0 400d08 4 6*0 400d08 4 6*0 400d08 4 6*0 400d08 4 6*0 400d08 4 6*0 400d08 4
  //   6*0 400d08 4 6*0 400d08 4 6*0 400d08 4 6*0 400d08 4 6*0 400d08 4 6*0 400d08 4 6*0 400d08 4 6*0
  //   400d08 4 6*0 400d08 4 6*0 400d08 4 6*0 400d08 4 6*0 400d08 4 6*0 400d08 4 6*0 400d08 4 6*0 400d08 4
  //   6*0 400d08 4 6*0 400d08 4 6*0 400d08 4 6*0 400d08 4 6*0 400d08 4 6*0 400d08 4
endmodule

module cpu (
  input  CLK,
  input  [7:0] DIN,
  input  INT,
  output [7:0] DOUT,
  output WE,
  output OE,
  output [15:0] ADDR
);

  wire [1:0] CTRL_a, CTRL_b, CTRL_c, CTRL_d;
  wire [2:0] CTRL_mm, CTRL_pc, CTRL_sp;
  wire [3:0] alu_1_z;
  wire [5:0] CTRL_alu;
  wire [7:0] CTRL_inr, multiplexer_2_out, register_1_q, register_2_q, register_3_q, register_4_q;
  wire [15:0] MM_out_7, PC_out_5, SP_out_5;

  // Probe on CTRL_inr
  // Probe on multiplexer_2_out
  Multiplexer #(.disabled("Z"), .width(8)) multiplexer_1 (.in1(multiplexer_2_out), .out(DOUT), .sel(WE));  // open: in0
  Multiplexer #(.disabled("Z"), .width(8)) multiplexer_2 (.in1(DIN), .out(multiplexer_2_out), .sel(OE));  // open: in0
  CTRL_CIRC CTRL (
    .Clk(CLK), .DATABUS(multiplexer_2_out), .FLAG(alu_1_z), .INT(INT), .out_5(ADDR), .MM(CTRL_mm),
    .PC(CTRL_pc), .SP(CTRL_sp), .D(CTRL_d), .C(CTRL_c), .B(CTRL_b), .A(CTRL_a), .ADR({OE, WE}),
    .ALU(CTRL_alu), .INR(CTRL_inr));
  PC_CIRC PC (.in_1(ADDR), .in_3(CTRL_pc), .in_2(CLK), .out_4(ADDR), .out_5(PC_out_5));
  // Probe on PC_out_5
  SP_CIRC SP (.in_1(ADDR), .in_3(CTRL_sp), .in_2(CLK), .out_4(ADDR), .out_5(SP_out_5));
  // Probe on SP_out_5
  MM_CIRC MM (
    .in_4(CTRL_mm), .in_1(ADDR), .in_2(multiplexer_2_out), .in_3(CLK), .out_5(multiplexer_2_out),
    .out_6(ADDR), .out_7(MM_out_7));
  // Probe on MM_out_7
  assign multiplexer_2_out = CTRL_a[0] ? register_1_q : 8'bz;  // Controlled_Buffer controlled_buffer_1
  Register register_1 (.D(multiplexer_2_out), .en(CTRL_a[1]), .Q(register_1_q), .clk(CLK));  // open: clr
  // Probe on ADDR
  assign multiplexer_2_out = CTRL_b[0] ? register_2_q : 8'bz;  // Controlled_Buffer controlled_buffer_2
  Register register_2 (.D(multiplexer_2_out), .en(CTRL_b[1]), .Q(register_2_q), .clk(CLK));  // open: clr
  ALU alu_1 (
    .A(register_1_q), .B(register_2_q), .cin(CTRL_alu[5]), .op3(CTRL_alu[4]), .op2(CTRL_alu[3]),
    .op1(CTRL_alu[2]), .op0(CTRL_alu[1]), .X(CTRL_alu[0]), .O(multiplexer_2_out), .Z(alu_1_z[0]),
    .G(alu_1_z[1]), .E(alu_1_z[2]), .C(alu_1_z[3]));
  assign multiplexer_2_out = CTRL_c[0] ? register_3_q : 8'bz;  // Controlled_Buffer controlled_buffer_3
  Register register_3 (.D(multiplexer_2_out), .en(CTRL_c[1]), .Q(register_3_q), .clk(CLK));  // open: clr
  assign multiplexer_2_out = CTRL_d[0] ? register_4_q : 8'bz;  // Controlled_Buffer controlled_buffer_4
  Register register_4 (.D(multiplexer_2_out), .en(CTRL_d[1]), .Q(register_4_q), .clk(CLK));  // open: clr
endmodule

module ALU (
  input  [7:0] A,
  input  [7:0] B,
  input  cin,
  input  op3,
  input  op2,
  input  op1,
  input  op0,
  input  X,
  output [7:0] O,
  output Z,
  output G,
  output E,
  output C
);

  wire adder_1_cout, subtractor_1_bout;
  wire [7:0] adder_1_out, and_1_out, demultiplexer_1_out0, demultiplexer_1_out1, demultiplexer_1_out2,
       demultiplexer_1_out3, demultiplexer_1_out4, demultiplexer_1_out5, demultiplexer_1_out6,
       demultiplexer_1_out7, demultiplexer_2_out0, demultiplexer_2_out1, demultiplexer_2_out2,
       demultiplexer_2_out3, demultiplexer_2_out4, demultiplexer_2_out6, demultiplexer_2_out7, not_1_out,
       or_1_out, shifter_1_out, shifter_2_out, subtractor_1_out, xor_1_out;

  Demultiplexer #(.select(3), .width(8)) demultiplexer_1 (
    .out0(demultiplexer_1_out0), .out1(demultiplexer_1_out1), .out2(demultiplexer_1_out2),
    .out3(demultiplexer_1_out3), .out4(demultiplexer_1_out4), .out5(demultiplexer_1_out5),
    .out6(demultiplexer_1_out6), .out7(demultiplexer_1_out7), .in(A), .sel({op2, op1, op0}));
  Demultiplexer #(.select(3), .width(8)) demultiplexer_2 (
    .out0(demultiplexer_2_out0), .out1(demultiplexer_2_out1), .out2(demultiplexer_2_out2),
    .out3(demultiplexer_2_out3), .out4(demultiplexer_2_out4), .out6(demultiplexer_2_out6),
    .out7(demultiplexer_2_out7), .in(B), .sel({op2, op1, op0}));  // open: out5
  Adder adder_1 (.a(demultiplexer_1_out0), .b(demultiplexer_2_out0), .out(adder_1_out), .cin(cin), .cout(adder_1_cout));
  Subtractor subtractor_1 (
    .a(demultiplexer_1_out1), .b(demultiplexer_2_out1), .out(subtractor_1_out), .bin(cin),
    .bout(subtractor_1_bout));
  assign and_1_out = demultiplexer_1_out2 & demultiplexer_2_out2;  // AND_Gate and_1, 8 bits wide
  assign or_1_out = demultiplexer_1_out3 | demultiplexer_2_out3;  // OR_Gate or_1, 8 bits wide
  assign xor_1_out = demultiplexer_1_out4 ^ demultiplexer_2_out4;  // XOR_Gate xor_1, 8 bits wide
  assign not_1_out = ~demultiplexer_1_out5;  // NOT_Gate not_1, 8 bits wide
  Shifter #(.shift("rl")) shifter_1 (
    .in(demultiplexer_1_out6), .\dist (demultiplexer_2_out6[2:0]), .out(shifter_1_out));
  Shifter #(.shift("rr")) shifter_2 (
    .in(demultiplexer_1_out7), .\dist (demultiplexer_2_out7[2:0]), .out(shifter_2_out));
  Multiplexer #(.disabled("Z"), .enable("true"), .select(3), .width(8)) multiplexer_1 (
    .in0(adder_1_out), .in1(subtractor_1_out), .in2(and_1_out), .in3(or_1_out), .in4(xor_1_out),
    .in5(not_1_out), .in6(shifter_1_out), .in7(shifter_2_out), .out(O), .sel({op2, op1, op0}), .en(X));
  nor nor_1 (Z, A[0], A[1], A[2], A[3], A[4], A[5], A[6], A[7]);
  Comparator comparator_1 (.a(A), .b(B), .gt(G), .eq(E));  // open: lt
  or or_2 (C, adder_1_cout, subtractor_1_bout);

  // Notes on the sheet:
  //   A: pull=down
  //   B: pull=down
endmodule

module CTRL_CIRC (
  input  INT,
  input  Clk,
  input  [7:0] DATABUS,
  input  [3:0] FLAG,
  output [15:0] out_5,
  output [2:0] MM,
  output [2:0] PC,
  output [2:0] SP,
  output [1:0] D,
  output [1:0] C,
  output [1:0] B,
  output [1:0] A,
  output [1:0] ADR,
  output [5:0] ALU,
  output [7:0] INR
);

  wire and_1_out, d_ff_1_q, j_k_ff_1_q, j_k_ff_1_qn, or_1_out;
  wire [2:0] controlled_buffer_1_out_2, counter_1_q, counter_2_q, CTRL;
  wire [3:0] and_2_out, decoder_1_out0, register_2_q;
  wire [11:11] or_2_out;
  wire [15:0] INTROM_data;
  wire [15:12] controlled_buffer_1_out;
  wire [31:0] INSTROM_data, pull_resistor_3_node;
  wire [31:22] multiplexer_1_out;

  and and_1 (and_1_out, INT, CTRL[2]);
  or or_1 (or_1_out, CTRL[2], controlled_buffer_1_out[15]);
  Register register_1 (.D(DATABUS), .en(CTRL[1]), .Q(INR), .clk(Clk));  // open: clr
  Register #(.width(4)) register_2 (.D(FLAG), .en(CTRL[0]), .Q(register_2_q), .clk(Clk));  // open: clr
  J_K_Flip_Flop #(.trigger("falling")) j_k_ff_1 (
    .J(controlled_buffer_1_out[15]), .clk(Clk), .K(and_1_out), .Q(j_k_ff_1_q), .Qn(j_k_ff_1_qn));  // open: preset, reset
  D_Flip_Flop #(.trigger("falling")) d_ff_1 (
    .clk(Clk), .D(or_1_out), .Q(d_ff_1_q), .reset(d_ff_1_q));  // open: Qn, preset
  Decoder #(.enable("false"), .select(2)) decoder_1 (
    .out0(decoder_1_out0[0]), .out1(decoder_1_out0[1]), .out2(decoder_1_out0[2]), .out3(decoder_1_out0[3]),
    .sel(INR[1:0]));
  Counter #(.max('h7), .trigger("falling"), .width(3)) counter_1 (
    .count(j_k_ff_1_qn), .Q(counter_1_q), .clk(Clk), .clr(d_ff_1_q));  // open: load, D, carry, up
  Counter #(.max('h7), .trigger("falling"), .width(3)) counter_2 (
    .count(j_k_ff_1_q), .Q(counter_2_q), .clk(Clk), .clr(d_ff_1_q));  // open: load, D, carry, up
  assign and_2_out = decoder_1_out0 & register_2_q;  // AND_Gate and_2, 4 bits wide
  or or_2 (or_2_out[11], and_2_out[0], and_2_out[1], and_2_out[2], and_2_out[3]);
  ROM #(.addrWidth(4), .dataWidth(16)) INTROM (.addr({INT, counter_1_q}), .data(INTROM_data));
  ROM #(.addrWidth(12), .dataWidth(32)) INSTROM (.addr({or_2_out[11], INR, counter_2_q}), .data(INSTROM_data));
  assign {controlled_buffer_1_out[15], pull_resistor_3_node[7:6], controlled_buffer_1_out[12], controlled_buffer_1_out_2, pull_resistor_3_node[26:24], pull_resistor_3_node[21:16]} = j_k_ff_1_qn ? INTROM_data : 16'bz;  // Controlled_Buffer controlled_buffer_1
  Pull_Resistor pull_resistor_1 (.node(INSTROM_data));
  Pull_Resistor pull_resistor_2 (.node({controlled_buffer_1_out[15], pull_resistor_3_node[7:6], controlled_buffer_1_out[12], controlled_buffer_1_out_2, pull_resistor_3_node[26:24], pull_resistor_3_node[21:16]}));
  Pull_Resistor pull_resistor_3 (.node(pull_resistor_3_node));
  Multiplexer #(.width(32)) multiplexer_1 (
    .in0(pull_resistor_3_node), .in1(INSTROM_data),
    .out({multiplexer_1_out[31:30], CTRL, MM, multiplexer_1_out[23:22], PC, SP, D, C, B, A, ADR, ALU}),
    .sel(j_k_ff_1_q));
  assign out_5 = controlled_buffer_1_out[12] ? {{13{1'b1}}, controlled_buffer_1_out_2} : 16'bz;  // Controlled_Buffer controlled_buffer_2

  // Notes on the sheet:
  //   Clk: pull=down
  //   contents of INTROM (hex, n*v repeats v):
  //   d010 f011 9010 b010
  //   contents of INSTROM (hex, n*v repeats v):
  //   aa00000 4000000 6*0 aa00000 7*0 aa00000 7*0 aa00000 7*0 aa00000 7*0 aa00000 7*0 aa00000 7*0 aa00000
  //   7*0 aa00000 4000000 6*0 aa00000 7*0 aa00000 7*0 aa00000 7*0 aa00000 7*0 aa00000 7*0 aa00000 7*0
  //   aa00000 7*0 aa00000 2a00100 4000000 5*0 aa00000 2a00200 4000000 5*0 aa00000 7*0 aa00000 7*0 aa00000
  //   7*0 aa00000 7*0 aa00000 7*0 aa00000 7*0 aa00000 7*0 aa00000 7*0 aa00000 7*0 aa00000 7*0 aa00000 7*0
  //   aa00000 7*0 aa00000 7*0 aa00000 7*0 aa00000 7*0 aa00000 7*0 aa00000 7*0 aa00000 7*0 aa00000 7*0
  //   aa00000 7*0 aa00000 7*0 aa00000 7*0 aa00000 7*0 aa00000 7*0 aa00000 7*0 aa00000 7*0 aa00000 7*0
  //   aa00000 7*0 aa00000 7*0 aa00000 7*0 aa00000 7*0 aa00000 7*0 aa00000 7*0 aa00000 7*0 aa00000 7*0
  //   aa00000 7*0 aa00000 7*0 aa00000 7*0 aa00000 7*0 aa00000 7*0 aa00000 7*0 aa00000 7*0 aa00000 7*0
  //   aa00000 7*0 aa00000 7*0 aa00000 7*0 aa00000 7*0 aa00000 7*0 aa00000 7*0 aa00000 7*0 aa00000 7*0
  //   aa00000 7*0 aa00000 7*0 aa00000 7*0 aa00000 7*0 aa00000 7*0 aa00000 7*0 aa00000 7*0 aa00000 7*0
  //   aa00000 7*0 aa00000 7*0 aa00000 7*0 aa00000 7*0 aa00000 7*0 aa00000 7*0 aa00000 7*0 aa00000 7*0
  //   aa00000 7*0 aa00000 7*0 aa00000 7*0 aa00000 7*0 aa00000 7*0 aa00000 7*0 aa00000 7*0 aa00000 7*0
  //   aa00000 7*0 aa00000 7*0 aa00000 7*0 aa00000 7*0 aa00000 7*0 aa00000 7*0 aa00000 7*0 aa00000 7*0
  //   aa00000 7*0 aa00000 7*0 aa00000 7*0 aa00000 7*0 aa00000 7*0 aa00000 7*0 aa00000 7*0 aa00000 7*0
  //   aa00000 7*0 aa00000 7*0 aa00000 7*0 aa00000 7*0 aa00000 7*0 aa00000 7*0 aa00000 7*0 aa00000 7*0
  //   aa00000 7*0 aa00000 7*0 aa00000 7*0 aa00000 7*0 aa00000 7*0 aa00000 7*0 aa00000 7*0 aa00000 7*0
  //   aa00000 7*0 aa00000 7*0 aa00000 7*0 aa00000 7*0 aa00000 7*0 aa00000 7*0 aa00000 7*0 aa00000 7*0
  //   aa00000 7*0 aa00000 7*0 aa00000 7*0 aa00000 7*0 aa00000 7*0 aa00000 7*0 aa00000 7*0 aa00000 7*0
  //   aa00000 7*0 aa00000 7*0 aa00000 7*0 aa00000 7*0 aa00000 7*0 aa00000 7*0 aa00000 7*0 aa00000 7*0
  //   aa00000 7*0 aa00000 7*0 aa00000 7*0 aa00000 7*0 aa00000 7*0 aa00000 7*0 aa00000 7*0 aa00000 7*0
  //   aa00000 7*0 aa00000 7*0 aa00000 7*0 aa00000 7*0 aa00000 7*0 aa00000 7*0 aa00000 7*0 aa00000 7*0
  //   aa00000 7*0 aa00000 7*0 aa00000 7*0 aa00000 7*0 aa00000 7*0 aa00000 7*0 aa00000 7*0 aa00000 7*0
  //   aa00000 7*0 aa00000 7*0 aa00000 7*0 aa00000 7*0 aa00000 7*0 aa00000 7*0 aa00000 7*0 aa00000 7*0
  //   aa00000 7*0 aa00000 7*0 aa00000 7*0 aa00000 7*0 aa00000 7*0 aa00000 7*0 aa00000 7*0 aa00000 7*0
  //   aa00000 7*0 aa00000 7*0 aa00000 7*0 aa00000 7*0 aa00000 7*0 aa00000 7*0 aa00000 7*0 aa00000 7*0
  //   aa00000 7*0 aa00000 7*0 aa00000 7*0 aa00000 7*0 aa00000 7*0 aa00000 7*0 aa00000 7*0 aa00000 7*0
  //   aa00000 7*0 aa00000 7*0 aa00000 7*0 aa00000 7*0 aa00000 7*0 aa00000 7*0 aa00000 7*0 aa00000 7*0
  //   aa00000 7*0 aa00000 7*0 aa00000 7*0 aa00000 7*0 aa00000 7*0 aa00000 7*0 aa00000 7*0 aa00000 7*0
  //   aa00000 7*0 aa00000 7*0 aa00000 7*0 aa00000 7*0 aa00000 7*0 aa00000 7*0 aa00000 7*0 aa00000 7*0
  //   aa00000 7*0 aa00000 7*0 aa00000 7*0 aa00000 7*0 aa00000 7*0 aa00000 7*0 aa00000 7*0 aa00000 7*0
  //   aa00000 7*0 aa00000 7*0 aa00000 7*0 aa00000 7*0 aa00000 7*0 aa00000 7*0 aa00000 7*0 aa00000 7*0
  //   aa00000 7*0 aa00000 7*0 aa00000 7*0 aa00000 7*0 aa00000 7*0 aa00000 7*0 aa00000 7*0 aa00000 7*0
  //   aa00000 7*0 aa00000 7*0 aa00000
endmodule

module bboard (
  input  [12:0] in_1,
  input  CE,
  input  [3:0] in_3,
  input  in_4,
  input  in_5,
  input  in_6
);

  wire clock_1_out, n74245_1_pin19, t_ff_1_q, undriven;
  wire [7:0] controlled_buffer_2_out, rom_1_data;
  wire [7:7] pull_resistor_1_node;
  wire [12:0] controlled_buffer_1_out;

  Clock clock_1 (.out(clock_1_out));
  T_Flip_Flop t_ff_1 (.clk(clock_1_out), .Q(t_ff_1_q));  // open: T, Qn, preset, reset
  T_Flip_Flop t_ff_2 (.clk(clock_1_out), .T(t_ff_1_q));  // open: Q, Qn, preset, reset
  Pull_Resistor pull_resistor_1 (.node(pull_resistor_1_node[7]));
  D_Flip_Flop #(.trigger("falling")) d_ff_1 (.preset(undriven));  // open: clk, D, Q, Qn, reset
  D_Flip_Flop #(.trigger("falling")) d_ff_2 (.preset(undriven));  // open: clk, D, Q, Qn, reset
  Register register_1 (.D({{3{pull_resistor_1_node[7]}}, in_4, in_3}), .en(in_5), .clk(in_6));  // open: Q, clr
  _74245 #(.ShowInternalStructure("true")) u_74245_1 (.pin19(n74245_1_pin19));  // open: pin1, pin2, pin3, pin4, pin5, pin6, pin7, pin8, pin9, pin18, pin17, pin16, pin15, pin14, pin13, pin12, pin11
  assign controlled_buffer_1_out = CE ? in_1 : 13'bz;  // Controlled_Buffer controlled_buffer_1
  assign controlled_buffer_2_out = CE ? rom_1_data : 8'bz;  // Controlled_Buffer controlled_buffer_2
  ROM #(.addrWidth(13)) rom_1 (.addr(controlled_buffer_1_out), .data(rom_1_data));
endmodule

module PC_CIRC (
  input  [15:0] in_1,
  input  in_2,
  input  [2:0] in_3,
  output [15:0] out_4,
  output [15:0] out_5
);

  wire and_1_out, and_2_out, and_3_out, counter_1_carry;

  and and_1 (and_1_out, in_3[1], in_3[0]);
  and and_2 (and_2_out, in_3[0], ~in_3[1]);  // AND_Gate
  Counter counter_1 (
    .load(and_2_out), .D(in_1[7:0]), .count(in_3[1]), .Q(out_5[7:0]), .carry(counter_1_carry),
    .up(and_1_out), .clk(in_2));  // open: clr
  and and_3 (and_3_out, counter_1_carry, in_3[1]);
  Counter counter_2 (
    .load(and_2_out), .D(in_1[15:8]), .count(and_3_out), .Q(out_5[15:8]), .up(and_1_out), .clk(in_2));  // open: carry, clr
  assign out_4 = in_3[2] ? out_5 : 16'bz;  // Controlled_Buffer controlled_buffer_1
endmodule

module SP_CIRC (
  input  [15:0] in_1,
  input  in_2,
  input  [2:0] in_3,
  output [15:0] out_4,
  output [15:0] out_5
);

  wire and_1_out, and_2_out, and_3_out, counter_1_carry;

  and and_1 (and_1_out, in_3[1], in_3[0]);
  and and_2 (and_2_out, in_3[0], ~in_3[1]);  // AND_Gate
  Counter counter_1 (
    .load(and_2_out), .D(in_1[7:0]), .count(in_3[1]), .Q(out_5[7:0]), .carry(counter_1_carry),
    .up(and_1_out), .clk(in_2));  // open: clr
  and and_3 (and_3_out, counter_1_carry, in_3[1]);
  Pull_Resistor pull_resistor_1 (.node(out_5[15:13]));
  Counter #(.max('h1f), .width(5)) counter_2 (
    .load(and_2_out), .D(in_1[12:8]), .count(and_3_out), .Q(out_5[12:8]), .up(and_1_out), .clk(in_2));  // open: carry, clr
  assign out_4 = in_3[2] ? out_5 : 16'bz;  // Controlled_Buffer controlled_buffer_1
endmodule

module MM_CIRC (
  input  [15:0] in_1,
  input  [7:0] in_2,
  input  in_3,
  input  [2:0] in_4,
  output [7:0] out_5,
  output [15:0] out_6,
  output [15:0] out_7
);

  wire decoder_1_out1, decoder_1_out2, decoder_1_out3, decoder_1_out5, decoder_1_out6, decoder_1_out7,
       or_1_out, or_2_out, or_3_out;
  wire [7:0] multiplexer_1_out, multiplexer_2_out;

  Decoder #(.enable("false"), .select(3)) decoder_1 (
    .out1(decoder_1_out1), .out2(decoder_1_out2), .out3(decoder_1_out3), .out5(decoder_1_out5),
    .out6(decoder_1_out6), .out7(decoder_1_out7), .sel(in_4));  // open: out0, out4
  Multiplexer #(.width(8)) multiplexer_1 (.in0(in_2), .in1(in_1[7:0]), .out(multiplexer_1_out), .sel(decoder_1_out1));
  or or_1 (or_1_out, decoder_1_out1, decoder_1_out2);
  or or_2 (or_2_out, decoder_1_out1, decoder_1_out3);
  or or_3 (or_3_out, decoder_1_out6, decoder_1_out7);
  Multiplexer #(.width(8)) multiplexer_2 (.in0(in_2), .in1(in_1[15:8]), .out(multiplexer_2_out), .sel(decoder_1_out1));
  Register register_1 (.D(multiplexer_1_out), .en(or_1_out), .Q(out_7[7:0]), .clk(in_3));  // open: clr
  Multiplexer #(.disabled("Z"), .enable("true"), .width(8)) multiplexer_3 (
    .in0(out_7[7:0]), .in1(out_7[15:8]), .out(out_5), .sel(decoder_1_out7), .en(or_3_out));
  Register register_2 (.D(multiplexer_2_out), .en(or_2_out), .Q(out_7[15:8]), .clk(in_3));  // open: clr
  assign out_6 = decoder_1_out5 ? out_7 : 16'bz;  // Controlled_Buffer controlled_buffer_1
endmodule
