// Logisim project CPU3.circ as structural Verilog
module main (
  input  [3:0] in_1,
  input  [1:0] in_2,
  input  [1:0] in_3,
  input  [3:0] in_4,
  input  [3:0] in_5,
  input  [3:0] in_6,
  input  [3:0] in_7,
  input  [3:0] in_8,
  input  [1:0] in_9,
  input  [5:0] in_10,
  input  Clk,
  output [15:0] out_12,
  output [7:0] out_13
);

  wire [1:0] demultiplexer_1_out0, demultiplexer_1_out1, demultiplexer_1_out2, demultiplexer_1_out3,
       demultiplexer_2_out0, demultiplexer_2_out1, demultiplexer_2_out2, demultiplexer_2_out3, or_1_out,
       or_2_out, or_3_out, or_4_out;
  wire [3:0] alu_1_alu_flg;
  wire [5:0] pla_1_out;
  wire [7:0] controlled_buffer_1_out, multiplexer_1_out, multiplexer_2_out, register_1_q, register_4_q,
       register_5_q, register_6_q, register_8_q, register_9_q, register_10_q, register_11_q, register_12_q;
  wire [15:0] controlled_buffer_8_out, counter_2_q, counter_3_q, register_7_q;

  assign controlled_buffer_1_out = or_1_out[0] ? register_1_q : 8'bz;  // Controlled_Buffer controlled_buffer_1
  Register register_1 (.D(controlled_buffer_1_out), .en(or_1_out[1]), .Q(register_1_q), .clk(Clk));  // open: clr
  assign or_1_out = demultiplexer_2_out3 | demultiplexer_1_out3;  // OR_Gate or_1, 2 bits wide
  Counter #(.max('hf), .width(4)) counter_1 (.clk(Clk));  // open: load, D, count, Q, carry, up, clr
  Register register_2 (.D(controlled_buffer_1_out), .clk(Clk));  // open: en, Q, clr
  Register #(.width(4)) register_3 (.D(alu_1_alu_flg), .clk(Clk));  // open: en, Q, clr
  assign controlled_buffer_1_out = or_2_out[0] ? register_4_q : 8'bz;  // Controlled_Buffer controlled_buffer_2
  Register register_4 (.D(controlled_buffer_1_out), .en(or_2_out[1]), .Q(register_4_q), .clk(Clk));  // open: clr
  assign or_2_out = demultiplexer_2_out2 | demultiplexer_1_out2;  // OR_Gate or_2, 2 bits wide
  assign controlled_buffer_1_out = or_3_out[0] ? register_5_q : 8'bz;  // Controlled_Buffer controlled_buffer_3
  Register register_5 (.D(controlled_buffer_1_out), .en(or_3_out[1]), .Q(register_5_q), .clk(Clk));  // open: clr
  assign or_3_out = demultiplexer_2_out1 | demultiplexer_1_out1;  // OR_Gate or_3, 2 bits wide
  assign controlled_buffer_1_out = or_4_out[0] ? register_6_q : 8'bz;  // Controlled_Buffer controlled_buffer_4
  Register register_6 (.D(controlled_buffer_1_out), .en(or_4_out[1]), .Q(register_6_q), .clk(Clk));  // open: clr
  assign or_4_out = demultiplexer_2_out0 | demultiplexer_1_out0;  // OR_Gate or_4, 2 bits wide
  Demultiplexer #(.select(2), .width(2)) demultiplexer_1 (
    .out0(demultiplexer_1_out0), .out1(demultiplexer_1_out1), .out2(demultiplexer_1_out2),
    .out3(demultiplexer_1_out3), .in(in_7[1:0]), .sel(in_6[1:0]));
  Demultiplexer #(.select(2), .width(2)) demultiplexer_2 (
    .out0(demultiplexer_2_out0), .out1(demultiplexer_2_out1), .out2(demultiplexer_2_out2),
    .out3(demultiplexer_2_out3), .in(in_7[3:2]), .sel(in_6[3:2]));
  PLA #(.in_width(4), .out_width(6), .\table ("xx01 000100\nxx10 010000\nxx11 010101\n01xx 001000\n10xx 100000\n11xx 101010\n0000 000000")) pla_1 (
    .in(in_8), .out(pla_1_out));
  assign out_12 = in_1[3] ? {{13{1'b1}}, in_1[2:0]} : 16'bz;  // Controlled_Buffer controlled_buffer_5
  assign out_12 = in_2[1] ? register_7_q : 16'bz;  // Controlled_Buffer controlled_buffer_6
  Register #(.width(16)) register_7 (
    .D(controlled_buffer_8_out), .en(in_2[0]), .Q(register_7_q), .clk(Clk));  // open: clr
  assign out_13 = in_3[1] ? register_8_q : 8'bz;  // Controlled_Buffer controlled_buffer_7
  Register register_8 (.D(controlled_buffer_1_out), .en(in_3[0]), .Q(register_8_q), .clk(Clk));  // open: clr
  assign controlled_buffer_8_out = in_4[3] ? counter_2_q : 16'bz;  // Controlled_Buffer controlled_buffer_8
  Counter #(.max('hffff), .width(16)) counter_2 (
    .load(in_4[1]), .D(controlled_buffer_8_out), .count(in_4[2]), .Q(counter_2_q), .up(in_4[0]), .clk(Clk));  // open: carry, clr
  Register register_9 (.D(controlled_buffer_1_out), .en(in_9[0]), .Q(register_9_q), .clk(Clk));  // open: clr
  Counter #(.max('hffff), .width(16)) counter_3 (
    .load(in_5[1]), .D(controlled_buffer_8_out), .count(in_5[2]), .Q(counter_3_q), .up(in_5[0]), .clk(Clk));  // open: carry, clr
  Multiplexer #(.width(8)) multiplexer_1 (
    .in0(controlled_buffer_1_out), .in1(controlled_buffer_8_out[15:8]), .out(multiplexer_1_out),
    .sel(pla_1_out[0]));
  Demultiplexer #(.disabled("Z"), .enable("true"), .tristate("true"), .width(8)) demultiplexer_3 (
    .out0(controlled_buffer_1_out), .out1(controlled_buffer_8_out[15:8]), .in(register_10_q),
    .sel(pla_1_out[1]), .en(pla_1_out[3]));
  Register register_10 (.D(multiplexer_1_out), .en(pla_1_out[2]), .Q(register_10_q), .clk(Clk));  // open: clr
  Register register_11 (.D(controlled_buffer_1_out), .en(in_9[1]), .Q(register_11_q), .clk(Clk));  // open: clr
  ALU alu_1 (
    .A(register_9_q), .B(register_11_q), .ALU_CTRL(in_10), .ALU_FLG(alu_1_alu_flg),
    .O(controlled_buffer_1_out));
  assign controlled_buffer_8_out = in_5[3] ? counter_3_q : 16'bz;  // Controlled_Buffer controlled_buffer_9
  Multiplexer #(.width(8)) multiplexer_2 (
    .in0(controlled_buffer_1_out), .in1(controlled_buffer_8_out[7:0]), .out(multiplexer_2_out),
    .sel(pla_1_out[0]));
  Demultiplexer #(.disabled("Z"), .enable("true"), .tristate("true"), .width(8)) demultiplexer_4 (
    .out0(controlled_buffer_1_out), .out1(controlled_buffer_8_out[7:0]), .in(register_12_q),
    .sel(pla_1_out[1]), .en(pla_1_out[5]));
  Register register_12 (.D(multiplexer_2_out), .en(pla_1_out[4]), .Q(register_12_q), .clk(Clk));  // open: clr
endmodule

module ALU (
  input  [5:0] ALU_CTRL,
  input  [7:0] A,
  input  [7:0] B,
  output [3:0] ALU_FLG,
  output [7:0] O
);

  wire adder_1_cout, nor_2_out, subtractor_1_bout;
  wire [3:0] bitadder_1_out, bitadder_2_out;
  wire [7:0] adder_1_out, and_1_out, even_parity_1_out, not_1_out, odd_parity_1_out, or_1_out, shifter_1_out,
       shifter_2_out, subtractor_1_out, xor_1_out;

  BitAdder bitadder_1 (.in0(A), .out(bitadder_1_out));
  assign and_1_out = A & B;  // AND_Gate and_1, 8 bits wide
  assign or_1_out = A | B;  // OR_Gate or_1, 8 bits wide
  assign not_1_out = ~A;  // NOT_Gate not_1, 8 bits wide
  nor nor_1 (ALU_FLG[3], bitadder_1_out[0], bitadder_1_out[1], bitadder_1_out[2], bitadder_1_out[3]);
  Comparator comparator_1 (.a(A), .b(B), .gt(ALU_FLG[2]), .eq(ALU_FLG[1]));  // open: lt
  Adder adder_1 (.a(A), .b(B), .out(adder_1_out), .cin(ALU_CTRL[5]), .cout(adder_1_cout));
  Multiplexer #(.enable("true")) multiplexer_1 (
    .in0(adder_1_cout), .in1(subtractor_1_bout), .out(ALU_FLG[0]), .sel(ALU_CTRL[0]), .en(nor_2_out));
  Subtractor subtractor_1 (.a(A), .b(B), .out(subtractor_1_out), .bin(ALU_CTRL[5]), .bout(subtractor_1_bout));
  Shifter #(.shift("rl")) shifter_1 (.in(A), .\dist (B[2:0]), .out(shifter_1_out));
  Shifter #(.shift("rr")) shifter_2 (.in(A), .\dist (B[2:0]), .out(shifter_2_out));
  assign xor_1_out = A ^ B;  // XOR_Gate xor_1, 8 bits wide
  assign odd_parity_1_out = A ^ B;  // Odd_Parity odd_parity_1, 8 bits wide
  assign even_parity_1_out = ~(A ^ B);  // Even_Parity even_parity_1, 8 bits wide
  BitAdder bitadder_2 (.in0(A), .out(bitadder_2_out));
  nor nor_2 (nor_2_out, ALU_CTRL[3], ALU_CTRL[2], ALU_CTRL[1]);
  Multiplexer #(.disabled("Z"), .enable("true"), .select(4), .width(8)) multiplexer_2 (
    .in1(adder_1_out), .in2(subtractor_1_out), .in3(shifter_1_out), .in4(shifter_2_out), .in5(and_1_out),
    .in6(or_1_out), .in7(xor_1_out), .in8(not_1_out), .in9(odd_parity_1_out), .in10(even_parity_1_out),
    .in11({4'b0000, bitadder_2_out}), .out(O), .sel(ALU_CTRL[3:0]), .en(ALU_CTRL[4]));  // open: in0, in12, in13, in14, in15
endmodule
